# Fritzing sketch RepresentationShema (saved by Fritzing 0.9.3b)
breadboards: 1

parts:
  Composant1 = Arduino Uno (Rev3)
  J2 = Basic Servo
  hc-sr1 = hc-sr04
  hc-sr2 = hc-sr04
  hc-sr3 = hc-sr04
  D1 = Rectifier Diode [part_number=1N4001 package="300 mil [THT]"]
  D2 = Rectifier Diode [part_number=1N4001 package="300 mil [THT]"]
  D3 = Rectifier Diode [part_number=1N4001 package="300 mil [THT]"]
  J3 = Basic Servo
  J1 = Basic Servo
  R1 = Resistor [tolerance=±5% resistance=220 package="0402 [SMD]"]
  R2 = Resistor [tolerance=±5% resistance=220 package="0402 [SMD]"]
  R3 = Resistor [tolerance=±5% resistance=220 package="0402 [SMD]"]
  R4 = Resistor [tolerance=±5% resistance=220 package="0402 [SMD]"]
  R5 = Photocell (LDR) [package=THT]
  R6 = Photocell (LDR) [package=THT]
  R7 = Photocell (LDR) [package=THT]
  R8 = Photocell (LDR) [package=THT]
  J4 = Piezo Speaker

nets:
  N1: Composant1.A0, R1.Pin_1, R5.pin_0
  N2: Composant1.A1, R2.Pin_1, R6.pin_0
  N3: Composant1.A2, R3.Pin_1, R7.pin_0
  N4: Composant1.A3, R4.Pin_1, R8.pin_0
  N5: Composant1.D8, hc-sr1.Trig
  N6: Composant1.D9_PWM, J4.pin2
  N7: Composant1.D10_PWM/SS, hc-sr2.Trig
  N8: Composant1.D11_PWM/MOSI, hc-sr3.Trig
  N9: Composant1.D12/MISO, D1.cathode, D2.cathode, D3.cathode
  N10: Composant1.D3_PWM, J1.pulse
  N11: Composant1.D5_PWM, J2.pulse
  N12: Composant1.D6_PWM, J3.pulse
  VCC: Composant1.5V, J2.vcc, J3.vcc, J1.vcc, R5.pin_1, R6.pin_1, R7.pin_1, R8.pin_1
  GND: Composant1.GND, J2.gnd, J3.gnd, J1.gnd, J4.pin1
  VCC_2: hc-sr1.VCC, hc-sr2.VCC, hc-sr3.VCC
  N13: hc-sr1.Echo, D3.anode
  GND_2: hc-sr1.GND, hc-sr2.GND, hc-sr3.GND, R1.Pin_0, R2.Pin_0, R3.Pin_0, R4.Pin_0
  N14: hc-sr2.Echo, D2.anode
  N15: hc-sr3.Echo, D1.anode
